# Fritzing sketch Lab_1_naive (saved by Fritzing 0.9.4)
breadboards: 1

parts:
  U1 = 7400 4 x 2 Input NAND Gate [part_number=7400 package="DIP (Dual Inline) [THT]"]
  S1 = Pushbutton [package=THT]
  S2 = Pushbutton [package=THT]
  S3 = Pushbutton [package=THT]
  R1 = Resistor [tolerance=±5% resistance=220 package=THT]
  R2 = Resistor [tolerance=±5% resistance=220 package=THT]
  R3 = Resistor [tolerance=±5% resistance=220 package=THT]
  R4 = Resistor [tolerance=±5% resistance=220 package=THT]
  LED1 = LED - 5mm [color="Red (633nm)" package="5 mm [THT]"]

nets:
  N1: U1.A1, S1.leg0, R1.Pin_0
  N2: U1.B1, U1.Q2, U1.A2, S2.leg0, R2.Pin_0
  N3: U1.Q1, U1.B3
  N4: U1.B2, U1.A4
  N5: U1.GND, R1.Pin_1, R2.Pin_1, R3.Pin_1, R4.Pin_1
  N6: U1.A3, LED1.cathode
  N7: U1.Q3, U1.Q4
  N8: U1.B4, S3.leg0, R3.Pin_0
  N9: U1.VDD, S1.leg1, S2.leg1, S3.leg1
  N10: R4.Pin_0, LED1.anode
