# Fritzing sketch Lab_1_redun (saved by Fritzing 0.9.4)
breadboards: 1

parts:
  S4 = Pushbutton [package=THT]
  S5 = Pushbutton [package=THT]
  S6 = Pushbutton [package=THT]
  R4 = Resistor [tolerance=±5% resistance=220 package=THT]
  R5 = Resistor [tolerance=±5% resistance=220 package=THT]
  R6 = Resistor [tolerance=±5% resistance=220 package=THT]
  U1 = 7400 4 x 2 Input NAND Gate [part_number=7400 package="DIP (Dual Inline) [THT]"]
  U2 = 7400 4 x 2 Input NAND Gate [part_number=7400 package="DIP (Dual Inline) [THT]"]
  LED2 = LED - 5mm [color="Red (633nm)" package="5 mm [THT]"]
  R7 = Resistor [tolerance=±5% resistance=220 package=THT]
  LED3 = LED - 5mm [color="Red (633nm)" package="5 mm [THT]"]
  R8 = Resistor [tolerance=±5% resistance=220 package=THT]

nets:
  N1: S4.leg0, R5.Pin_0, U1.Q3, U2.A1, U2.B1
  VDD: S4.leg1, S5.leg1, S6.leg1, U1.VDD, U2.VDD
  N2: S5.leg0, R6.Pin_0, U1.A1
  N3: S6.leg0, R4.Pin_0, U1.B1, U1.Q2, U1.A2
  GND: R4.Pin_1, R5.Pin_1, R6.Pin_1, U1.GND, U2.GND, R7.Pin_1, R8.Pin_1
  N4: U1.Q1, U1.B4
  N5: U1.B2, U1.B3
  N6: U1.A3, U1.A4
  N7: U1.Q4, U2.A4, U2.B4, LED3.cathode
  N8: U2.Q1, U2.B3
  N9: U2.A3, LED2.cathode
  N10: U2.Q3, U2.Q4
  N11: LED2.anode, R7.Pin_0
  N12: LED3.anode, R8.Pin_0
