# Fritzing sketch Lab2 Fritz (saved by Fritzing 0.9.4)
breadboards: 3

parts:
  U2 = 7400 4 x 2 Input NAND Gate [part_number=7400 package="DIP (Dual Inline) [THT]"]
  U3 = 7402 4 x 2 Input NOR Gate [part_number=7402 package="DIP (Dual Inline) [THT]"]
  U4 = 7486 4 x 2 Input XOR Gate [part_number=7486 package="DIP (Dual Inline) [THT]"]
  U5 = 7404 Hex Inverter [part_number=7404 package=dil14]
  U6 = 74151 8:1 MUX [part_number=74151 package="DIP16 [THT]"]
  U7 = 74194 4 Bit Bi-Directional Shift Register [part_number=74194 package="DIP16 [THT]"]
  U8 = 74194 4 Bit Bi-Directional Shift Register [part_number=74194 package="DIP16 [THT]"]
  U9 = 74153 Dual 4:1 MUX [part_number=74153 package="DIP16 [THT]"]
  U10 = 74161 4 Bit Synchronous Up Down Counter [part_number=74161 package="DIP16 [THT]"]
  U11 = 7402 4 x 2 Input NOR Gate [part_number=7402 package="DIP (Dual Inline) [THT]"]
  U12 = 7474 Dual Positive Edge Triggered D Flip Flop [part_number=7474 package="DIP (Dual Inline) [THT]"]
  U13 = 7427 3 x 3 Input NOR Gate [part_number=7427 package="DIP (Dual Inline) [THT]"]

nets:
  N1: U2.A1, U3.B1, U4.A1, U7.13, U9.A0, U9.B0, U9.D1
  N2: U2.B1, U3.Q1, U4.B1, U5.2A, U8.12, U9.D0, U9.C1, U9.A1
  N3: U2.Q1, U5.1A, U6.15
  GND: U2.GND, U3.GND, U4.GND, U5.GND, U9.G0, U9.GND
  N4: U2.A4, U5.4A
  N5: U2.B4, U12.B2, U13.A2
  VDD: U2.VDD, U3.VDD, U4.VDD, U5.VCC, U9.VCC, U10.1, U12.Q2
  N6: U3.A1, U6.14
  N7: U4.Q1, U5.3A, U6.2
  N8: U5.1Y, U6.4
  N9: U5.2Y, U6.3
  N10: U5.3Y, U6.13
  N11: U5.4Y, U12.B1
  N12: U5.5Y, U13.B3
  N13: U5.6Y, U11.Q1, U11.A4
  N14: U5.6A, U13.A3
  GND_2: U6.1, U6.7, U6.GND, U10.GND, U12.GND
  N15: U6.5, U9.C0, U9.B1
  VCC: U6.12, U6.VCC, U10.VCC, U12.VDD
  N16: U7.2, U9.Y0
  N17: U7.3, U8.3
  N18: U7.4, U8.4
  N19: U7.5, U8.5
  N20: U7.6, U8.6
  GND_3: U7.GND, U8.GND, U11.GND
  N21: U7.9, U11.Q2
  N22: U7.10, U11.B1
  N23: U7.11, U8.11, U10.2, U12.Q1
  VCC_2: U7.VCC, U8.VCC, U11.VDD
  N24: U8.2, U9.Y1
  N25: U8.9, U11.Q3
  N26: U8.10, U11.Q4
  N27: U10.7, U10.10
  N28: U10.13, U13.Q2, U13.Q3
  N29: U10.14, U13.Q1, U13.Q4
  N30: U11.A1, U11.A2, U11.B2
  N31: U11.A3, U11.B3, U11.B4

custom parts:
  7404 Hex Inverter: 74XX04 Hex Inverter, Modified by Zuofu Cheng (Aug 2020)
  74151 8:1 MUX: 74151 8:1 Multiplexor
  74153 Dual 4:1 MUX: 74153 Dual 4:1 Multiplexor
  7427 3 x 3 Input NOR Gate: 7427 3 x 2 Input NOR Gate
